# Fritzing sketch interfaccia_sensore (saved by Fritzing 0.9.3b)
circuit board: 4.0989cm x 2.71322cm
perfboards: 1

parts:
  C1 = Electrolytic Capacitor [capacitance=100nF package="100 mil [THT, electrolytic]"]
  J1 = female pin header, 4 pins [form="♀ (female)" part_number="Connettore Sensore"]
  J2 = screw terminal, 4 pins [part_number="Connettore cavi"]

nets:
  N1: C1.-, J1.pin4, J2.pin4
  N2: C1.+, J1.pin1, J2.pin1
  N3: J1.pin2, J2.pin2
  N4: J1.pin3, J2.pin3

notes:
  Interfaccia sensore livello, 1
